// Logisim project s-mips.circ as structural Verilog
module S_MIPS_Board (
  input  DESHABILITAR_DISPATCHER,
  output halt
);

  wire button_1_out, CLK, CS, d_ff_1_q, LCLR, LoadRAM, LoadRAMOn, LW, R_R_W, R_W, ram_dispatcher_1_finished,
       RCS, Reset_out, RST, TTY_EN;
  wire [2:0] KDB;
  wire [3:0] LMask, Mask, ram_1_read_time, ram_1_write_time, RMask;
  wire [6:0] KDB_DATA, TTY_DATA;
  wire [15:0] Addr, LAddr, RAddr;
  wire [31:0] I0, I1, I2, I3, LData, ram_1_data_out_0, ram_1_data_out_1, ram_1_data_out_2, ram_1_data_out_3,
       RI0, RI1, RI2, RI3;

  TTY #(.rows(25), .cols(80)) tty_1 (.data(TTY_DATA), .clk(CLK), .we(TTY_EN), .clr(RST));
  not not_1 (LoadRAMOn, ram_dispatcher_1_finished);
  RAM_Dispatcher ram_dispatcher_1 (
    .WriteTime(ram_1_write_time), .Clock(CLK), .Data(LData), .Address(LAddr), .Mask(LMask),
    .Finished(ram_dispatcher_1_finished), .Write(LW), .CLR(LCLR));
  Keyboard #(.buflen(64)) keyboard_1 (.clk(CLK), .re(KDB[0]), .avail(KDB[2]), .data(KDB_DATA));  // open: clr
  RAM ram_1 (
    .Address(RAddr), .Data_Out_0(ram_1_data_out_0), .Data_Out_1(ram_1_data_out_1),
    .Data_Out_2(ram_1_data_out_2), .Data_Out_3(ram_1_data_out_3), .Data_In_0(RI0), .Data_In_1(RI1),
    .Data_In_2(RI2), .Data_In_3(RI3), .Mask(RMask), .nRead_Write(R_R_W), .Chip_Select(RCS),
    .Read_Time(ram_1_read_time), .Reset(button_1_out), .Write_Time(ram_1_write_time));
  Button button_1 (.out(button_1_out));
  D_Flip_Flop d_ff_1 (.clk(CLK), .D(1'b1), .Q(d_ff_1_q), .reset(Reset_out));  // open: Qn, preset, en
  Button Reset (.out(Reset_out));
  S_MIPS s_mips_1 (
    .Kbd_Enable(KDB[0]), .Address(Addr), .Kbd_Clear(KDB[1]), .Kbd_Available(KDB[2]), .RAM_In_0(I0),
    .Kbd_ASCII_Data(KDB_DATA), .RAM_In_1(I1), .TTY_Enable(TTY_EN), .RAM_In_2(I2), .RAM_In_3(I3),
    .TTY_ASCII_Data(TTY_DATA), .Reset(RST), .RAM_Out_0(ram_1_data_out_0), .Clock(CLK),
    .RAM_Out_1(ram_1_data_out_1), .Stop(halt), .RAM_Out_2(ram_1_data_out_2), .RAM_Out_3(ram_1_data_out_3),
    .Mask(Mask), .Read_Time(ram_1_read_time), .Write_Time(ram_1_write_time), .nRead_Write(R_W),
    .Chip_Select(CS));
  D_Flip_Flop d_ff_2 (.clk(CLK), .D(d_ff_1_q), .Qn(LCLR), .reset(Reset_out));  // open: Q, preset, en
  or or_1 (RST, LCLR, LoadRAM);
  Clock clock_1 (.out(CLK));
  Multiplexer #(.width(32), .enable("false")) multiplexer_1 (.in0(I0), .in1(LData), .out(RI0), .sel(LoadRAM));
  Multiplexer #(.width(32), .enable("false")) multiplexer_2 (.in0(I1), .in1(LData), .out(RI1), .sel(LoadRAM));
  Multiplexer #(.width(32), .enable("false")) multiplexer_3 (.in0(I2), .in1(LData), .out(RI2), .sel(LoadRAM));
  Multiplexer #(.width(32), .enable("false")) multiplexer_4 (.in0(I3), .in1(LData), .out(RI3), .sel(LoadRAM));
  and and_1 (LoadRAM, ~DESHABILITAR_DISPATCHER, LoadRAMOn);  // AND_Gate
  Multiplexer #(.width(16), .enable("false")) multiplexer_5 (.in0(Addr), .in1(LAddr), .out(RAddr), .sel(LoadRAM));
  Multiplexer #(.width(4), .enable("false")) multiplexer_6 (.in0(Mask), .in1(LMask), .out(RMask), .sel(LoadRAM));
  Multiplexer #(.enable("false")) multiplexer_7 (.in0(CS), .in1(LW), .out(RCS), .sel(LoadRAM));
  Multiplexer #(.enable("false")) multiplexer_8 (.in0(R_W), .in1(LW), .out(R_R_W), .sel(LoadRAM));

  // Notes on the sheet:
  //   NO MODIFICAR
  //   Keyboard
endmodule

module RAM (
  input  [15:0] Address,
  input  [31:0] Data_In_0,
  input  [31:0] Data_In_1,
  input  [31:0] Data_In_2,
  input  [31:0] Data_In_3,
  input  [3:0] Mask,
  input  nRead_Write,
  input  Chip_Select,
  input  Reset,
  output [31:0] Data_Out_0,
  output [31:0] Data_Out_1,
  output [31:0] Data_Out_2,
  output [31:0] Data_Out_3,
  output [3:0] Read_Time,
  output [3:0] Write_Time
);

  wire and_2_out, and_3_out, and_4_out, and_5_out, and_6_out, and_7_out, and_8_out, and_9_out, Changed, CLK,
       comparator_2_eq, comparator_3_eq, comparator_4_eq, comparator_5_eq, comparator_6_eq, Count,
       demultiplexer_3_out0, Idle, Idle_q, Load, Load0, Load1, nand_1_out, or_1_out, or_2_out, or_3_out,
       or_4_out, or_5_out, or_6_out, or_7_out, or_8_out, or_9_out, or_10_out, Proc_q, Update_Mem, Zero_Time;
  wire [3:0] counter_1_q, multiplexer_1_out, subtractor_1_out;
  wire [31:0] register_1_q, register_2_q, register_3_q, register_4_q, register_5_q;

  // Probe on 4'b0011
  // Probe on 4'b0010
  Multiplexer #(.width(4), .enable("false")) multiplexer_1 (
    .in0(4'b0011), .in1(4'b0010), .out(multiplexer_1_out), .sel(nRead_Write));
  or or_1 (or_1_out, Idle, Update_Mem);
  or or_2 (or_2_out, ~Chip_Select, Reset);  // OR_Gate
  Subtractor #(.width(4)) subtractor_1 (.a(multiplexer_1_out), .b(4'b0010), .out(subtractor_1_out));  // open: bin, bout
  D_Flip_Flop u_Idle (.clk(CLK), .D(or_1_out), .Q(Idle_q), .preset(or_2_out));  // open: Qn, en, reset
  Demultiplexer #(.enable("false")) demultiplexer_1 (.out0(Idle), .out1(Load0), .in(Idle_q), .sel(Changed));
  // Probe on counter_1_q
  Counter #(.width(4), .max('hf)) counter_1 (
    .load(Load), .D(subtractor_1_out), .count(Count), .Q(counter_1_q), .clk(CLK), .clr(or_3_out));  // open: carry
  or or_3 (or_3_out, ~Chip_Select, Reset);  // OR_Gate
  Comparator #(.width(4), .mode("unsigned")) comparator_1 (
    .a(4'b0000), .b(counter_1_q), .eq(Zero_Time));  // open: gt, lt
  or or_4 (or_4_out, Count, Load0, Load1);
  Register #(.width(32)) register_1 (.D(Data_In_0), .en(Chip_Select), .Q(register_1_q), .clk(CLK), .clr(or_5_out));
  or or_5 (or_5_out, ~Chip_Select, Reset);  // OR_Gate
  Register #(.width(32)) register_2 (.D(Data_In_1), .en(Chip_Select), .Q(register_2_q), .clk(CLK), .clr(or_6_out));
  or or_6 (or_6_out, ~Chip_Select, Reset);  // OR_Gate
  Register #(.width(32)) register_3 (.D(Data_In_2), .en(Chip_Select), .Q(register_3_q), .clk(CLK), .clr(or_7_out));
  or or_7 (or_7_out, ~Chip_Select, Reset);  // OR_Gate
  Register #(.width(32)) register_4 (.D(Data_In_3), .en(Chip_Select), .Q(register_4_q), .clk(CLK), .clr(or_8_out));
  or or_8 (or_8_out, ~Chip_Select, Reset);  // OR_Gate
  Register #(.width(32)) register_5 (
    .D({{11{1'b1}}, nRead_Write, Mask, Address}), .en(Chip_Select), .Q(register_5_q), .clk(CLK),
    .clr(or_9_out));
  or or_9 (or_9_out, ~Chip_Select, Reset);  // OR_Gate
  D_Flip_Flop Proc (.clk(CLK), .D(or_4_out), .Q(Proc_q), .reset(or_10_out));  // open: Qn, preset, en
  or or_10 (or_10_out, ~Chip_Select, Reset);  // OR_Gate
  Demultiplexer #(.enable("false")) demultiplexer_2 (
    .out0(Count), .out1(Update_Mem), .in(demultiplexer_3_out0), .sel(Zero_Time));
  Demultiplexer #(.enable("false")) demultiplexer_3 (
    .out0(demultiplexer_3_out0), .out1(Load1), .in(Proc_q), .sel(Changed));
  Clock clock_1 (.out(CLK));
  Comparator #(.width(32)) comparator_2 (.a(register_1_q), .b(Data_In_0), .eq(comparator_2_eq));  // open: gt, lt
  Comparator #(.width(32)) comparator_3 (.a(register_2_q), .b(Data_In_1), .eq(comparator_3_eq));  // open: gt, lt
  Comparator #(.width(32)) comparator_4 (.a(register_3_q), .b(Data_In_2), .eq(comparator_4_eq));  // open: gt, lt
  Comparator #(.width(32)) comparator_5 (.a(register_4_q), .b(Data_In_3), .eq(comparator_5_eq));  // open: gt, lt
  Comparator #(.width(32)) comparator_6 (
    .a(register_5_q), .b({{11{1'b1}}, nRead_Write, Mask, Address}), .eq(comparator_6_eq));  // open: gt, lt
  nand nand_1 (nand_1_out, comparator_6_eq, comparator_2_eq, comparator_3_eq, comparator_4_eq, comparator_5_eq);
  and and_1 (Changed, nand_1_out, Chip_Select);
  or or_11 (Load, Count, Load1, Load0);
  and and_2 (and_2_out, Mask[0], Update_Mem, nRead_Write);
  and and_3 (and_3_out, Mask[1], Update_Mem, nRead_Write);
  and and_4 (and_4_out, Mask[2], Update_Mem, nRead_Write);
  and and_5 (and_5_out, Mask[3], Update_Mem, nRead_Write);
  RAM_part #(.addrWidth(16), .dataWidth(32), .bus("separate")) ram_1 (
    .addr(Address), .din(Data_In_0), .data(Data_Out_0), .str(and_2_out), .sel(Chip_Select), .clk(CLK),
    .ld(and_6_out), .clr(Reset));
  and and_6 (and_6_out, ~nRead_Write, Idle);  // AND_Gate
  RAM_part #(.addrWidth(16), .dataWidth(32), .bus("separate")) ram_2 (
    .addr(Address), .din(Data_In_1), .data(Data_Out_1), .str(and_3_out), .sel(Chip_Select), .clk(CLK),
    .ld(and_7_out), .clr(Reset));
  and and_7 (and_7_out, ~nRead_Write, Idle);  // AND_Gate
  RAM_part #(.addrWidth(16), .dataWidth(32), .bus("separate")) ram_3 (
    .addr(Address), .din(Data_In_2), .data(Data_Out_2), .str(and_4_out), .sel(Chip_Select), .clk(CLK),
    .ld(and_8_out), .clr(Reset));
  and and_8 (and_8_out, ~nRead_Write, Idle);  // AND_Gate
  RAM_part #(.addrWidth(16), .dataWidth(32), .bus("separate")) ram_4 (
    .addr(Address), .din(Data_In_3), .data(Data_Out_3), .str(and_5_out), .sel(Chip_Select), .clk(CLK),
    .ld(and_9_out), .clr(Reset));
  and and_9 (and_9_out, ~nRead_Write, Idle);  // AND_Gate

  assign Read_Time = 4'b0011;
  assign Write_Time = 4'b0010;

  // Other names for the same wires on the sheet: M0 = Mask[0]; M1 = Mask[1]; M2 = Mask[2]; M3 = Mask[3];
  //   RW = nRead_Write; CLR = Reset; CS = Chip_Select; Load2 = Count

  // Notes on the sheet:
  //   NO MODIFICAR
  //   excepto quizás los valores RT y WT
  //   BANK0
  //   BANK1
  //   BANK2
  //   BANK3
endmodule

module RAM_Dispatcher (
  input  [3:0] WriteTime,
  input  Clock,
  input  CLR,
  output [31:0] Data,
  output [15:0] Address,
  output [3:0] Mask,
  output Finished,
  output Write
);

  wire demultiplexer_2_out1, demultiplexer_3_out1, End, IDLE_q, IncAddr, Load, or_1_out, or_2_out, While_q,
       WriteEnd;
  wire [3:0] counter_1_q;
  wire [31:0] CurrentAddress_q;

  Counter #(.width(32), .max('hffffffff)) CurrentAddress (
    .count(IncAddr), .Q({CurrentAddress_q[31:18], Address, CurrentAddress_q[1:0]}), .clk(Clock), .clr(CLR));  // open: load, D, carry
  or or_1 (or_1_out, IncAddr, demultiplexer_3_out1, Finished);
  D_Flip_Flop IDLE (.clk(Clock), .D(or_1_out), .Q(IDLE_q), .preset(CLR));  // open: Qn, en, reset
  Demultiplexer #(.enable("false")) demultiplexer_1 (.out0(Load), .out1(Finished), .in(IDLE_q), .sel(End));
  D_Flip_Flop While (.clk(Clock), .D(or_2_out), .Q(While_q), .reset(CLR));  // open: Qn, preset, en
  or or_2 (or_2_out, Write, Load);
  RAM_part #(.addrWidth(18), .dataWidth(32)) ram_1 (
    .addr({Address, CurrentAddress_q[1:0]}), .data(Data), .clk(Clock));  // open: sel, ld, clr
  Demultiplexer #(.enable("false")) demultiplexer_2 (
    .out0(Write), .out1(demultiplexer_2_out1), .in(While_q), .sel(WriteEnd));
  Decoder #(.select(2)) decoder_1 (
    .out0(Mask[0]), .out1(Mask[1]), .out2(Mask[2]), .out3(Mask[3]), .sel(CurrentAddress_q[1:0]));  // open: en
  Demultiplexer #(.enable("false")) demultiplexer_3 (
    .out0(IncAddr), .out1(demultiplexer_3_out1), .in(demultiplexer_2_out1), .sel(End));
  Counter #(.width(4), .max('hf)) counter_1 (
    .load(Load), .D(WriteTime), .count(Write), .Q(counter_1_q), .clk(Clock));  // open: carry, clr
  Comparator #(.width(32)) comparator_1 (.a(Data), .b({32{1'b1}}), .eq(End));  // open: gt, lt
  Comparator #(.width(4)) comparator_2 (.a(4'b0000), .b(counter_1_q), .eq(WriteEnd));  // open: gt, lt

  // Other names for the same wires on the sheet: CLK = Clock; Count = Write; WT[3:0] = WriteTime
endmodule

module S_MIPS (
  input  Kbd_Available,
  input  [6:0] Kbd_ASCII_Data,
  input  [31:0] RAM_Out_0,
  input  [31:0] RAM_Out_1,
  input  Reset,
  input  [31:0] RAM_Out_2,
  input  Clock,
  input  [31:0] RAM_Out_3,
  input  [3:0] Read_Time,
  input  [3:0] Write_Time,
  output Kbd_Enable,
  output [15:0] Address,
  output Kbd_Clear,
  output TTY_Enable,
  output [6:0] TTY_ASCII_Data,
  output Stop,
  output [31:0] RAM_In_0,
  output [31:0] RAM_In_1,
  output [31:0] RAM_In_2,
  output [31:0] RAM_In_3,
  output [3:0] Mask,
  output nRead_Write,
  output Chip_Select
);

  // Cache cache_1: pin names not known; wires that end beside it: Chip_Select, nRead_Write

  // Other names for the same wires on the sheet: CLK = Clock; CLR = Reset; CS = Chip_Select;
  //   KBD_AVAIL = Kbd_Available; KBD_CLR = Kbd_Clear; KBD_DATA[6:0] = Kbd_ASCII_Data; RAM_A[15:0] = Address;
  //   RAM_INPUT_0[31:0] = RAM_In_0; RAM_INPUT_1[31:0] = RAM_In_1; RAM_INPUT_2[31:0] = RAM_In_2;
  //   RAM_INPUT_3[31:0] = RAM_In_3; RAM_MASK[3:0] = Mask; RAM_OUTPUT_0[31:0] = RAM_Out_0;
  //   RAM_OUTPUT_1[31:0] = RAM_Out_1; RAM_OUTPUT_2[31:0] = RAM_Out_2; RAM_OUTPUT_3[31:0] = RAM_Out_3;
  //   RW = nRead_Write; TTY_DATA[6:0] = TTY_ASCII_Data

  // Notes on the sheet:
  //   RAM ADDRESS
  //   DATA FROM RAM
  //   DATA TO RAM
  //   DATA WRITE MASK
  //   RAM TIMING
  //   RAM CONTROL
  //   KEYBOARD
  //   TTY
  //   SEQUENCING
endmodule

module CU (
  input  [2:0] Operation,
  input  Clock,
  input  Reset,
  input  Inmediate,
  input  Unsigned,
  output Control_Branch_Jump,
  output Re_Write_Register_Value,
  output Chng_Value,
  output Chng_Selector,
  output Write_from_Hi_Lo,
  output Chng_Sig
);

  wire Chng_Sig1, Chng_Sig2, d_ff_1_q, d_ff_2_q, demultiplexer_1_out0, demultiplexer_1_out1,
       demultiplexer_1_out2, demultiplexer_1_out3, demultiplexer_1_out4, demultiplexer_1_out5,
       demultiplexer_1_out6, Next1, Next2, or_1_out, or_4_out, or_5_out;

  or or_1 (or_1_out, d_ff_1_q, Control_Branch_Jump);
  D_Flip_Flop #(.trigger("falling")) d_ff_1 (
    .clk(Clock), .D(1'b0), .Q(d_ff_1_q), .preset(Reset));  // open: Qn, en, reset
  or or_2 (Chng_Sig, Chng_Sig1, Chng_Sig2);
  D_Flip_Flop #(.trigger("falling")) d_ff_2 (
    .clk(Clock), .D(or_1_out), .Q(d_ff_2_q), .reset(Reset));  // open: Qn, preset, en
  Demultiplexer #(.select(3)) demultiplexer_1 (
    .out0(demultiplexer_1_out0), .out1(demultiplexer_1_out1), .out2(demultiplexer_1_out2),
    .out3(demultiplexer_1_out3), .out4(demultiplexer_1_out4), .out5(demultiplexer_1_out5),
    .out6(demultiplexer_1_out6), .in(d_ff_2_q), .sel(Operation));  // open: out7, en
  buf or_3 (Re_Write_Register_Value, Next1);  // OR_Gate
  or or_4 (or_4_out, demultiplexer_1_out0, or_5_out);
  or or_5 (or_5_out, Next1, Next2, Write_from_Hi_Lo);
  D_Flip_Flop #(.trigger("falling")) d_ff_3 (
    .clk(Clock), .D(demultiplexer_1_out2), .Q(Next2), .reset(Reset));  // open: Qn, preset, en
  D_Flip_Flop #(.trigger("falling")) d_ff_4 (
    .clk(Clock), .D(demultiplexer_1_out3), .Q(Write_from_Hi_Lo), .reset(Reset));  // open: Qn, preset, en
  D_Flip_Flop #(.trigger("falling")) d_ff_5 (
    .clk(Clock), .D(demultiplexer_1_out4), .reset(Reset));  // open: Q, Qn, preset, en
  D_Flip_Flop #(.trigger("falling")) d_ff_6 (
    .clk(Clock), .D(demultiplexer_1_out5), .reset(Reset));  // open: Q, Qn, preset, en
  D_Flip_Flop #(.trigger("falling")) d_ff_7 (
    .clk(Clock), .D(demultiplexer_1_out6), .reset(Reset));  // open: Q, Qn, preset, en
  D_Flip_Flop #(.trigger("falling")) d_ff_8 (
    .clk(Clock), .D(or_4_out), .Q(Control_Branch_Jump), .reset(Reset));  // open: Qn, preset, en
  D_Flip_Flop #(.trigger("falling")) d_ff_9 (
    .clk(Clock), .D(demultiplexer_1_out1), .Q(Next1), .reset(Reset));  // open: Qn, preset, en
  and and_1 (Chng_Selector, Inmediate, Next1);
  and and_2 (Chng_Value, Inmediate, Next1);
  and and_3 (Chng_Sig2, Unsigned, Next2);
  and and_4 (Chng_Sig1, Unsigned, Next1);

  // Other names for the same wires on the sheet: Chng_Sel = Chng_Selector; Chng_Val = Chng_Value;
  //   End = Control_Branch_Jump; Jmp = Control_Branch_Jump; RW1 = Next1; Next3 = Write_from_Hi_Lo;
  //   Wr_from_Hi_Lo = Write_from_Hi_Lo

  // Notes on the sheet:
  //   Idle
  //   Start
  //   Salto
  //   Aritmetica-Logica-Comparativa
  //   Multiplicacion/Division
  //   Register-Move
  //   Memory
  //   Ram Memory
  //   Actualizar el PC con la orden de saltar
  //   End
  //   Cambiar el input B,  la instuccion del ALU de ser inmediato y de signo
  //   Guardar valor en el registro correspondiente
  //   Cambiar el signo de los valores
  //   Escribir al registro por defecto Rd de Hi/Lo
endmodule

module Cache (
  input  Clock,
  input  [3:0] Read_Time,
  input  [3:0] Write_Time,
  input  [31:0] Address,
  input  [31:0] Ram_Input_00,
  input  [31:0] Ram_Input_01,
  input  [31:0] Ram_Input_02,
  input  [31:0] Ram_Input_03,
  input  [31:0] Change_Addr,
  input  [31:0] Change_Value,
  input  WriteRam,
  output Wait,
  output CS,
  output NR_W,
  output [31:0] Output,
  output [15:0] Current_Addr,
  output [3:0] Mask,
  output WriteClear
);

  wire Ad0, Ad1, Ad2, Ad3, and_6_out, and_7_out, and_8_out, and_9_out, comparator_1_eq, comparator_2_eq,
       comparator_3_eq, comparator_4_eq, cronometro_1_finish, CS0, demultiplexer_2_out0,
       demultiplexer_2_out1, demultiplexer_2_out2, demultiplexer_2_out3, En, En0, En1, En2, En3, Rp0, Rp1,
       Rp2, Rp3, UpdOff;
  wire [1:0] Out, UpdOut;
  wire [7:0] R00, R00W, R01, R01W, R02, R02W, R03, R03W, R10, R10W, R11, R11W, R12, R12W, R13, R13W, R20,
       R20W, R21, R21W, R22, R22W, R23, R23W, R30, R30W, R31, R31W, R32, R32W, R33, R33W, W00, W01, W02, W03,
       W10, W11, W12, W13, W20, W21, W22, W23, W30, W31, W32, W33;
  wire [27:0] Tag;

  Register #(.width(28), .trigger("falling")) register_1 (
    .D(Address[31:4]), .en(En), .Q(Tag), .clk(Clock));  // open: clr
  nor nor_1 (CS0, Ad0, Ad1, Ad2, Ad3);
  Demultiplexer #(.select(2), .width(32)) demultiplexer_1 (
    .out0({R00W, R01W, R02W, R03W}), .out1({R10W, R11W, R12W, R13W}), .out2({R20W, R21W, R22W, R23W}),
    .out3({R30W, R31W, R32W, R33W}), .in(Change_Value), .sel(UpdOut));  // open: en
  Register #(.trigger("falling")) register_2 (.D(R00), .en(En0), .Q(W00), .clk(Clock));  // open: clr
  Register #(.trigger("falling")) register_3 (.D(R10), .en(En1), .Q(W10), .clk(Clock));  // open: clr
  Register #(.trigger("falling")) register_4 (.D(R20), .en(En2), .Q(W20), .clk(Clock));  // open: clr
  Register #(.trigger("falling")) register_5 (.D(R30), .en(En3), .Q(W30), .clk(Clock));  // open: clr
  Comparator #(.width(30)) comparator_1 (
    .a({Tag, 2'b00}), .b(Change_Addr[31:2]), .eq(comparator_1_eq));  // open: gt, lt
  Comparator #(.width(30)) comparator_2 (
    .a({Tag, 2'b01}), .b(Change_Addr[31:2]), .eq(comparator_2_eq));  // open: gt, lt
  Comparator #(.width(30)) comparator_3 (
    .a({Tag, 2'b10}), .b(Change_Addr[31:2]), .eq(comparator_3_eq));  // open: gt, lt
  Comparator #(.width(30)) comparator_4 (
    .a({Tag, 2'b11}), .b(Change_Addr[31:2]), .eq(comparator_4_eq));  // open: gt, lt
  Comparator #(.width(30)) comparator_5 (.a({Tag, 2'b00}), .b(Address[31:2]), .eq(Ad0));  // open: gt, lt
  Comparator #(.width(30)) comparator_6 (.a({Tag, 2'b01}), .b(Address[31:2]), .eq(Ad1));  // open: gt, lt
  Comparator #(.width(30)) comparator_7 (.a({Tag, 2'b10}), .b(Address[31:2]), .eq(Ad2));  // open: gt, lt
  Comparator #(.width(30)) comparator_8 (.a({Tag, 2'b11}), .b(Address[31:2]), .eq(Ad3));  // open: gt, lt
  Cronometro cronometro_1 (.Time(Read_Time), .Start(CS0), .Clock(Clock), .Finish(cronometro_1_finish));
  and and_1 (Rp0, WriteRam, comparator_1_eq);
  and and_2 (Rp1, WriteRam, comparator_2_eq);
  and and_3 (Rp2, WriteRam, comparator_3_eq);
  and and_4 (Rp3, WriteRam, comparator_4_eq);
  Register #(.trigger("falling")) register_6 (.D(R01), .en(En0), .Q(W01), .clk(Clock));  // open: clr
  Register #(.trigger("falling")) register_7 (.D(R11), .en(En1), .Q(W11), .clk(Clock));  // open: clr
  Register #(.trigger("falling")) register_8 (.D(R21), .en(En2), .Q(W21), .clk(Clock));  // open: clr
  Register #(.trigger("falling")) register_9 (.D(R31), .en(En3), .Q(W31), .clk(Clock));  // open: clr
  or or_1 (Wait, CS0, WriteRam);
  and and_5 (En, cronometro_1_finish, CS0);
  Multiplexer #(.width(8)) multiplexer_1 (.in0(Ram_Input_00[7:0]), .in1(R03W), .out(R03), .sel(WriteRam));  // open: en
  Multiplexer #(.width(8)) multiplexer_2 (.in0(Ram_Input_00[15:8]), .in1(R02W), .out(R02), .sel(WriteRam));  // open: en
  Multiplexer #(.width(8)) multiplexer_3 (
    .in0(Ram_Input_00[23:16]), .in1(R01W), .out(R01), .sel(WriteRam));  // open: en
  Multiplexer #(.width(8)) multiplexer_4 (
    .in0(Ram_Input_00[31:24]), .in1(R00W), .out(R00), .sel(WriteRam));  // open: en
  or or_2 (CS, WriteRam, CS0);
  Priority_Encoder #(.select(2)) priority_encoder_1 (
    .in0(Rp0), .in1(Rp1), .in2(Rp2), .in3(Rp3), .out(UpdOut), .en_out(UpdOff));  // open: gs, en_in
  Register #(.trigger("falling")) register_10 (.D(R02), .en(En0), .Q(W02), .clk(Clock));  // open: clr
  Register #(.trigger("falling")) register_11 (.D(R12), .en(En1), .Q(W12), .clk(Clock));  // open: clr
  Register #(.trigger("falling")) register_12 (.D(R22), .en(En2), .Q(W22), .clk(Clock));  // open: clr
  Register #(.trigger("falling")) register_13 (.D(R32), .en(En3), .Q(W32), .clk(Clock));  // open: clr
  Priority_Encoder #(.select(2)) priority_encoder_2 (
    .in0(Ad0), .in1(Ad1), .in2(Ad2), .in3(Ad3), .out(Out));  // open: gs, en_out, en_in
  Multiplexer #(.width(8)) multiplexer_5 (.in0(Ram_Input_01[7:0]), .in1(R13W), .out(R13), .sel(WriteRam));  // open: en
  Multiplexer #(.width(8)) multiplexer_6 (.in0(Ram_Input_01[15:8]), .in1(R12W), .out(R12), .sel(WriteRam));  // open: en
  Multiplexer #(.width(8)) multiplexer_7 (
    .in0(Ram_Input_01[23:16]), .in1(R11W), .out(R11), .sel(WriteRam));  // open: en
  Multiplexer #(.width(8)) multiplexer_8 (
    .in0(Ram_Input_01[31:24]), .in1(R10W), .out(R10), .sel(WriteRam));  // open: en
  Multiplexer #(.width(16)) multiplexer_9 (
    .in0(Address[19:4]), .in1(Change_Addr[19:4]), .out(Current_Addr), .sel(WriteRam));  // open: en
  Decoder #(.select(2)) decoder_1 (
    .out0(Mask[3]), .out1(Mask[2]), .out2(Mask[1]), .out3(Mask[0]), .sel(Change_Addr[3:2]));  // open: en
  Demultiplexer #(.select(2)) demultiplexer_2 (
    .out0(demultiplexer_2_out0), .out1(demultiplexer_2_out1), .out2(demultiplexer_2_out2),
    .out3(demultiplexer_2_out3), .in(WriteRam), .sel(UpdOut));  // open: en
  Register #(.trigger("falling")) register_14 (.D(R03), .en(En0), .Q(W03), .clk(Clock));  // open: clr
  Register #(.trigger("falling")) register_15 (.D(R13), .en(En1), .Q(W13), .clk(Clock));  // open: clr
  Register #(.trigger("falling")) register_16 (.D(R23), .en(En2), .Q(W23), .clk(Clock));  // open: clr
  Register #(.trigger("falling")) register_17 (.D(R33), .en(En3), .Q(W33), .clk(Clock));  // open: clr
  Multiplexer #(.width(8)) multiplexer_10 (.in0(Ram_Input_02[7:0]), .in1(R23W), .out(R23), .sel(WriteRam));  // open: en
  Multiplexer #(.width(8)) multiplexer_11 (
    .in0(Ram_Input_02[15:8]), .in1(R22W), .out(R22), .sel(WriteRam));  // open: en
  Multiplexer #(.width(8)) multiplexer_12 (
    .in0(Ram_Input_02[23:16]), .in1(R21W), .out(R21), .sel(WriteRam));  // open: en
  Multiplexer #(.width(8)) multiplexer_13 (
    .in0(Ram_Input_02[31:24]), .in1(R20W), .out(R20), .sel(WriteRam));  // open: en
  Cronometro cronometro_2 (.Time(Write_Time), .Start(WriteRam), .Clock(Clock), .Finish(WriteClear));
  Multiplexer #(.select(2), .width(32)) multiplexer_14 (
    .in0({W03, W02, W01, W00}), .in1({W13, W12, W11, W10}), .in2({W23, W22, W21, W20}),
    .in3({W33, W32, W31, W30}), .out(Output), .sel(Out));  // open: en
  and and_6 (and_6_out, ~UpdOff, demultiplexer_2_out0);  // AND_Gate
  and and_7 (and_7_out, ~UpdOff, demultiplexer_2_out1);  // AND_Gate
  and and_8 (and_8_out, ~UpdOff, demultiplexer_2_out2);  // AND_Gate
  and and_9 (and_9_out, ~UpdOff, demultiplexer_2_out3);  // AND_Gate
  Multiplexer #(.width(8)) multiplexer_15 (.in0(Ram_Input_03[7:0]), .in1(R33W), .out(R33), .sel(WriteRam));  // open: en
  Multiplexer #(.width(8)) multiplexer_16 (
    .in0(Ram_Input_03[15:8]), .in1(R32W), .out(R32), .sel(WriteRam));  // open: en
  Multiplexer #(.width(8)) multiplexer_17 (
    .in0(Ram_Input_03[23:16]), .in1(R31W), .out(R31), .sel(WriteRam));  // open: en
  Multiplexer #(.width(8)) multiplexer_18 (
    .in0(Ram_Input_03[31:24]), .in1(R30W), .out(R30), .sel(WriteRam));  // open: en
  or or_3 (En0, En, and_6_out);
  or or_4 (En1, En, and_7_out);
  or or_5 (En2, En, and_8_out);
  or or_6 (En3, En, and_9_out);

  assign NR_W = WriteRam;

  // Other names for the same wires on the sheet: Addr[31:0] = Address; Addr1[15:0] = Address[19:4];
  //   CTag[27:0] = Address[31:4]; Chng[31:0] = Change_Addr; Addr2[15:0] = Change_Addr[19:4]; Clk = Clock;
  //   R03R[7:0] = Ram_Input_00[7:0]; R02R[7:0] = Ram_Input_00[15:8]; R01R[7:0] = Ram_Input_00[23:16];
  //   R00R[7:0] = Ram_Input_00[31:24]; R13R[7:0] = Ram_Input_01[7:0]; R12R[7:0] = Ram_Input_01[15:8];
  //   R11R[7:0] = Ram_Input_01[23:16]; R10R[7:0] = Ram_Input_01[31:24]; R23R[7:0] = Ram_Input_02[7:0];
  //   R22R[7:0] = Ram_Input_02[15:8]; R21R[7:0] = Ram_Input_02[23:16]; R20R[7:0] = Ram_Input_02[31:24];
  //   R33R[7:0] = Ram_Input_03[7:0]; R32R[7:0] = Ram_Input_03[15:8]; R31R[7:0] = Ram_Input_03[23:16];
  //   R30R[7:0] = Ram_Input_03[31:24]; RT[3:0] = Read_Time; Wait1 = CS0; CS1 = WriteRam; Update = WriteRam;
  //   Wait2 = WriteRam; WT[3:0] = Write_Time

  // Notes on the sheet:
  //   Suponiendo que sea la direccion correcta
  //   div 16
  //   No coincide Buscar
  //   Offset
  //   Index
  //   00
  //   01
  //   10
  //   11
  //   div 4
  //   Detener CU
  //   Compare
  //   Comparar si el valor a cambiar tiene direccion igual a los datos de la cache
  //   Esperar Tiempo de escritura
  //   Si coincide
  //   Insertar en Ram
  //   Enable
  //   Salida
endmodule

module Cronometro (
  input  [3:0] Time,
  input  Start,
  input  Clock,
  output Finish
);

  wire Reset;
  wire [3:0] counter_1_q;

  Counter #(.width(4), .max('hf)) counter_1 (
    .count(Start), .Q(counter_1_q), .clk(Clock), .clr(Reset));  // open: load, D, carry
  Comparator #(.width(4), .mode("unsigned")) comparator_1 (.a(Time), .b(counter_1_q), .eq(Finish));  // open: gt, lt
  D_Flip_Flop d_ff_1 (.clk(Clock), .D(Finish), .Q(Reset), .reset(Reset));  // open: Qn, preset, en

  // Other names for the same wires on the sheet: Clk = Clock
endmodule

module DataPath_2 (
  input  [5:0] Funct_Code,
  input  [5:0] I_Funct_Code,
  input  Clock,
  input  Inmediate,
  input  RW,
  input  WfromHi_Lo,
  input  SelHi_Lo,
  input  [4:0] Rs,
  input  [4:0] Rt,
  input  [4:0] Rd,
  input  [15:0] Const,
  output [31:0] RS_Val,
  output beq,
  output bne,
  output bgtz,
  output blez,
  output bltz
);

  wire Hi_Lo_W, not_1_out;
  wire [3:0] alu_decoder_1_output;
  wire [4:0] multiplexer_2_out;
  wire [31:0] High_Value, Low_Value, multiplexer_1_out, multiplexer_3_out, multiplexer_4_out, R_Input,
       register_file_1_hi, register_file_1_low, register_file_1_outpu2, sign_extender_1_output;

  Multiplexer #(.width(32)) multiplexer_1 (
    .in0(multiplexer_3_out), .in1(R_Input), .out(multiplexer_1_out), .sel(not_1_out));  // open: en
  not not_1 (not_1_out, WfromHi_Lo);
  Multiplexer #(.width(5)) multiplexer_2 (.in0(Rd), .in1(Rt), .out(multiplexer_2_out), .sel(Inmediate));  // open: en
  Register_file register_file_1 (
    .Clock(Clock), .Input(multiplexer_1_out), .RW(RW), .Select(multiplexer_2_out), .B(Rt),
    .Outpu2(register_file_1_outpu2), .Output1(RS_Val), .A(Rs), .Hi_Lo_W(Hi_Lo_W), .Hi_Input(High_Value),
    .Low_Input(Low_Value), .Hi(register_file_1_hi), .Low(register_file_1_low));
  Multiplexer #(.width(32)) multiplexer_3 (
    .in0(register_file_1_low), .in1(register_file_1_hi), .out(multiplexer_3_out), .sel(SelHi_Lo));  // open: en
  // Probe on multiplexer_4_out
  Sign_Extender sign_extender_1 (.Input(Const), .Output(sign_extender_1_output));
  // Probe on RS_Val
  Multiplexer #(.width(32)) multiplexer_4 (
    .in0(register_file_1_outpu2), .in1(sign_extender_1_output), .out(multiplexer_4_out), .sel(Inmediate));  // open: en
  ALU alu_1 (
    .in_1(RS_Val), .in_2(multiplexer_4_out), .Clock(Clock), .in_4(alu_decoder_1_output), .out_5(R_Input),
    .Hi_Res(High_Value), .Low_Res(Low_Value));  // open: beq, bne, bgtz, blez, bltz
  ALU_Decoder alu_decoder_1 (
    .Funct_Code(Funct_Code), .Output(alu_decoder_1_output), .I_Funct_Code(I_Funct_Code), .in_3(Inmediate),
    .WHi_Lo(Hi_Lo_W));
  // Probe on alu_decoder_1_output
  // Probe on Low_Value
  // Probe on R_Input
  // Probe on High_Value

  // Other names for the same wires on the sheet: Clk = Clock; F_Code[5:0] = Funct_Code; I_F_Code[5:0] = I_Funct_Code;
  //   Inm = Inmediate; SHi = SelHi_Lo; Wr_from_Hi_Lo = WfromHi_Lo
endmodule

module Register_file (
  input  Clock,
  input  [31:0] Input,
  input  [31:0] Hi_Input,
  input  [31:0] Low_Input,
  input  RW,
  input  Hi_Lo_W,
  input  [4:0] Select,
  input  [4:0] A,
  input  [4:0] B,
  output [31:0] Hi,
  output [31:0] Low,
  output [31:0] Output1,
  output [31:0] Outpu2
);

  wire D0, D1, D2, D3, D4, D5, D6, D7, D8, D9, D10, D11, D12, D13, D14, D15, D16, D17, D18, D19, D20, D21,
       D22, D23, D24, D25, D26, D27, D28, D29, D30, D31, E0, E1, E2, E3, E4, E5, E6, E7, E8, E9, E10, E11,
       E12, E13, E14, E15, E16, E17, E18, E19, E20, E21, E22, E23, E24, E25, E26, E27, E28, E29, E30, E31;
  wire [31:0] S0, S1, S2, S3, S4, S5, S6, S7, S8, S9, S10, S11, S12, S13, S14, S15, S16, S17, S18, S19, S20,
       S21, S22, S23, S24, S25, S26, S27, S28, S29, S30, S31;

  Decoder #(.select(5)) decoder_1 (
    .out0(D0), .out1(D1), .out2(D2), .out3(D3), .out4(D4), .out5(D5), .out6(D6), .out7(D7), .out8(D8),
    .out9(D9), .out10(D10), .out11(D11), .out12(D12), .out13(D13), .out14(D14), .out15(D15), .out16(D16),
    .out17(D17), .out18(D18), .out19(D19), .out20(D20), .out21(D21), .out22(D22), .out23(D23), .out24(D24),
    .out25(D25), .out26(D26), .out27(D27), .out28(D28), .out29(D29), .out30(D30), .out31(D31), .sel(Select));  // open: en
  Register #(.width(32)) u_Hi (.D(Hi_Input), .en(Hi_Lo_W), .Q(Hi), .clk(Clock));  // open: clr
  Register #(.width(32)) u_Low (.D(Low_Input), .en(Hi_Lo_W), .Q(Low), .clk(Clock));  // open: clr
  and and_1 (E0, RW, D0);
  and and_2 (E1, RW, D1);
  and and_3 (E2, RW, D2);
  and and_4 (E3, RW, D3);
  and and_5 (E4, RW, D4);
  and and_6 (E5, RW, D5);
  and and_7 (E6, RW, D6);
  and and_8 (E7, RW, D7);
  Multiplexer #(.select(5), .width(32)) multiplexer_1 (
    .in0(S0), .in1(S1), .in2(S2), .in3(S3), .in4(S4), .in5(S5), .in6(S6), .in7(S7), .in8(S8), .in9(S9),
    .in10(S10), .in11(S11), .in12(S12), .in13(S13), .in14(S14), .in15(S15), .in16(S16), .in17(S17),
    .in18(S18), .in19(S19), .in20(S20), .in21(S21), .in22(S22), .in23(S23), .in24(S24), .in25(S25),
    .in26(S26), .in27(S27), .in28(S28), .in29(S29), .in30(S30), .in31(S31), .out(Output1), .sel(A));  // open: en
  Multiplexer #(.select(5), .width(32)) multiplexer_2 (
    .in0(S0), .in1(S1), .in2(S2), .in3(S3), .in4(S4), .in5(S5), .in6(S6), .in7(S7), .in8(S8), .in9(S9),
    .in10(S10), .in11(S11), .in12(S12), .in13(S13), .in14(S14), .in15(S15), .in16(S16), .in17(S17),
    .in18(S18), .in19(S19), .in20(S20), .in21(S21), .in22(S22), .in23(S23), .in24(S24), .in25(S25),
    .in26(S26), .in27(S27), .in28(S28), .in29(S29), .in30(S30), .in31(S31), .out(Outpu2), .sel(B));  // open: en
  and and_9 (E8, RW, D8);
  and and_10 (E9, RW, D9);
  and and_11 (E10, RW, D10);
  and and_12 (E11, RW, D11);
  and and_13 (E12, RW, D12);
  and and_14 (E13, RW, D13);
  and and_15 (E14, RW, D14);
  and and_16 (E15, RW, D15);
  Register #(.width(32)) R0 (.D(Input), .en(1'b0), .Q(S0), .clk(Clock));  // open: clr
  Register #(.width(32)) R8 (.D(Input), .en(E8), .Q(S8), .clk(Clock));  // open: clr
  Register #(.width(32)) R16 (.D(Input), .en(E16), .Q(S16), .clk(Clock));  // open: clr
  Register #(.width(32)) R24 (.D(Input), .en(E24), .Q(S24), .clk(Clock));  // open: clr
  Register #(.width(32)) R1 (.D(Input), .en(E1), .Q(S1), .clk(Clock));  // open: clr
  Register #(.width(32)) R9 (.D(Input), .en(E9), .Q(S9), .clk(Clock));  // open: clr
  Register #(.width(32)) R17 (.D(Input), .en(E17), .Q(S17), .clk(Clock));  // open: clr
  Register #(.width(32)) R25 (.D(Input), .en(E25), .Q(S25), .clk(Clock));  // open: clr
  and and_17 (E16, RW, D16);
  and and_18 (E17, RW, D17);
  and and_19 (E18, RW, D18);
  and and_20 (E19, RW, D19);
  and and_21 (E20, RW, D20);
  and and_22 (E21, RW, D21);
  and and_23 (E22, RW, D22);
  and and_24 (E23, RW, D23);
  Register #(.width(32)) R2 (.D(Input), .en(E2), .Q(S2), .clk(Clock));  // open: clr
  Register #(.width(32)) R10 (.D(Input), .en(E10), .Q(S10), .clk(Clock));  // open: clr
  Register #(.width(32)) R18 (.D(Input), .en(E18), .Q(S18), .clk(Clock));  // open: clr
  Register #(.width(32)) R26 (.D(Input), .en(E26), .Q(S26), .clk(Clock));  // open: clr
  and and_25 (E24, RW, D24);
  and and_26 (E25, RW, D25);
  and and_27 (E26, RW, D26);
  and and_28 (E27, RW, D27);
  and and_29 (E28, RW, D28);
  and and_30 (E29, RW, D29);
  and and_31 (E30, RW, D30);
  and and_32 (E31, RW, D31);
  Register #(.width(32)) R3 (.D(Input), .en(E3), .Q(S3), .clk(Clock));  // open: clr
  Register #(.width(32)) R11 (.D(Input), .en(E11), .Q(S11), .clk(Clock));  // open: clr
  Register #(.width(32)) R19 (.D(Input), .en(E19), .Q(S19), .clk(Clock));  // open: clr
  Register #(.width(32)) R27 (.D(Input), .en(E27), .Q(S27), .clk(Clock));  // open: clr
  Register #(.width(32)) R4 (.D(Input), .en(E4), .Q(S4), .clk(Clock));  // open: clr
  Register #(.width(32)) R12 (.D(Input), .en(E12), .Q(S12), .clk(Clock));  // open: clr
  Register #(.width(32)) R20 (.D(Input), .en(E20), .Q(S20), .clk(Clock));  // open: clr
  Register #(.width(32)) R28 (.D(Input), .en(E28), .Q(S28), .clk(Clock));  // open: clr
  Register #(.width(32)) R5 (.D(Input), .en(E5), .Q(S5), .clk(Clock));  // open: clr
  Register #(.width(32)) R13 (.D(Input), .en(E13), .Q(S13), .clk(Clock));  // open: clr
  Register #(.width(32)) R21 (.D(Input), .en(E21), .Q(S21), .clk(Clock));  // open: clr
  Register #(.width(32)) R29 (.D(Input), .en(E29), .Q(S29), .clk(Clock));  // open: clr
  Register #(.width(32)) R6 (.D(Input), .en(E6), .Q(S6), .clk(Clock));  // open: clr
  Register #(.width(32)) R14 (.D(Input), .en(E14), .Q(S14), .clk(Clock));  // open: clr
  Register #(.width(32)) R22 (.D(Input), .en(E22), .Q(S22), .clk(Clock));  // open: clr
  Register #(.width(32)) R30 (.D(Input), .en(E30), .Q(S30), .clk(Clock));  // open: clr
  Register #(.width(32)) R7 (.D(Input), .en(E7), .Q(S7), .clk(Clock));  // open: clr
  Register #(.width(32)) R15 (.D(Input), .en(E15), .Q(S15), .clk(Clock));  // open: clr
  Register #(.width(32)) R23 (.D(Input), .en(E23), .Q(S23), .clk(Clock));  // open: clr
  Register #(.width(32)) R31 (.D(Input), .en(E31), .Q(S31), .clk(Clock));  // open: clr

  // Other names for the same wires on the sheet: A_t[31:0] = Input; CL = Clock; H_L_R = Hi_Lo_W
endmodule

module ALU (
  input  [31:0] in_1,
  input  [31:0] in_2,
  input  Clock,
  input  [3:0] in_4,
  output [31:0] out_5,
  output beq,
  output bne,
  output bgtz,
  output blez,
  output bltz,
  output [31:0] Hi_Res,
  output [31:0] Low_Res
);

  wire comparator_1_gt, comparator_2_gt, comparator_4_eq, multiplexer_2_out;
  wire [1:0] M_D;
  wire [31:0] add_circuit_1_output, and_1_out, divider_1_out, divider_1_rem, divider_2_out, divider_2_rem,
       multiplexer_1_out, multiplier_1_cout, multiplier_1_out, multiplier_2_cout, multiplier_2_out,
       nor_1_out, or_1_out, Random, sub_circuit_1_output, xor_1_out;

  Random #(.width(32)) random_1 (.clk(Clock), .next(1'b1), .out(Random));  // open: clr
  Add_Circuit add_circuit_1 (.A(in_1), .B(in_2), .Output(add_circuit_1_output));  // open: OverFlow, C_out
  Sub_Circuit sub_circuit_1 (.A(in_1), .B(in_2), .Output(sub_circuit_1_output));  // open: OverFlow, B_out
  assign and_1_out = in_1 & in_2;  // AND_Gate and_1, 32 bits wide
  assign or_1_out = in_1 | in_2;  // OR_Gate or_1, 32 bits wide
  assign nor_1_out = ~(in_1 | in_2);  // NOR_Gate nor_1, 32 bits wide
  assign xor_1_out = in_1 ^ in_2;  // XOR_Gate xor_1, 32 bits wide
  Comparator #(.width(32)) comparator_1 (.a(in_1), .b(in_2), .gt(comparator_1_gt));  // open: eq, lt
  Comparator #(.width(32), .mode("unsigned")) comparator_2 (.a(in_1), .b(in_2), .gt(comparator_2_gt));  // open: eq, lt
  Comparator #(.width(32)) comparator_3 (.a(in_1), .b(in_2), .eq(beq));  // open: gt, lt
  Multiplier #(.width(32)) multiplier_1 (
    .a(in_1), .b(in_2), .out(multiplier_1_out), .cout(multiplier_1_cout));  // open: cin
  Multiplier #(.width(32)) multiplier_2 (
    .a(in_1), .b(in_2), .out(multiplier_2_out), .cout(multiplier_2_cout));  // open: cin
  Divider #(.width(32)) divider_1 (.a(in_1), .b(in_2), .out(divider_1_out), .rem(divider_1_rem));  // open: upper
  Divider #(.width(32)) divider_2 (.a(in_1), .b(in_2), .out(divider_2_out), .rem(divider_2_rem));  // open: upper
  not not_1 (bne, beq);
  Comparator #(.width(32)) comparator_4 (.a(in_1), .b({32{1'b0}}), .gt(bgtz), .eq(comparator_4_eq), .lt(bltz));
  Multiplexer #(.width(32)) multiplexer_1 (
    .in0({32{1'b0}}), .in1(32'h1), .out(multiplexer_1_out), .sel(multiplexer_2_out));  // open: en
  Multiplexer multiplexer_2 (
    .in0(comparator_1_gt), .in1(comparator_2_gt), .out(multiplexer_2_out), .sel(in_4[0]));  // open: en
  or or_2 (blez, comparator_4_eq, bltz);
  Multiplexer #(.select(2), .width(32)) multiplexer_3 (
    .in0(multiplier_1_out), .in1(multiplier_2_out), .in2(divider_1_out), .in3(divider_2_out), .out(Low_Res),
    .sel(M_D));  // open: en
  Multiplexer #(.select(2), .width(32)) multiplexer_4 (
    .in0(multiplier_1_cout), .in1(multiplier_2_cout), .in2(divider_1_rem), .in3(divider_2_rem), .out(Hi_Res),
    .sel(M_D));  // open: en
  Subtractor #(.width(2)) subtractor_1 (.a(in_4[1:0]), .b(2'b10), .out(M_D));  // open: bin, bout
  Multiplexer #(.select(4), .width(32)) multiplexer_5 (
    .in0(add_circuit_1_output), .in1(sub_circuit_1_output), .in6(and_1_out), .in7(or_1_out), .in8(nor_1_out),
    .in9(xor_1_out), .in10(multiplexer_1_out), .in11(multiplexer_1_out), .in12(Random), .out(out_5),
    .sel(in_4));  // open: in2, in3, in4, in5, in13, in14, in15, en

  // Other names for the same wires on the sheet: Equal = beq; NoEqual = bne; OP[3:0] = in_4
endmodule

module ALU_Decoder (
  input  [5:0] Funct_Code,
  input  [5:0] I_Funct_Code,
  input  in_3,
  output WHi_Lo,
  output [3:0] Output
);

  wire comparator_1_eq, comparator_2_eq, comparator_3_eq, comparator_4_eq, comparator_5_eq, comparator_6_eq,
       comparator_7_eq, comparator_8_eq, comparator_9_eq, comparator_10_eq, comparator_11_eq,
       comparator_12_eq, comparator_13_eq;
  wire [5:0] Code;

  Multiplexer #(.width(6)) multiplexer_1 (.in0(Funct_Code), .in1(I_Funct_Code), .out(Code), .sel(in_3));  // open: en
  Comparator #(.width(6), .mode("unsigned")) comparator_1 (
    .a(Code), .b(6'b100000), .eq(comparator_1_eq));  // open: gt, lt
  Comparator #(.width(6), .mode("unsigned")) comparator_2 (
    .a(Code), .b(6'b100010), .eq(comparator_2_eq));  // open: gt, lt
  Comparator #(.width(6), .mode("unsigned")) comparator_3 (
    .a(Code), .b(6'b011000), .eq(comparator_3_eq));  // open: gt, lt
  Comparator #(.width(6), .mode("unsigned")) comparator_4 (
    .a(Code), .b(6'b011001), .eq(comparator_4_eq));  // open: gt, lt
  Comparator #(.width(6), .mode("unsigned")) comparator_5 (
    .a(Code), .b(6'b011010), .eq(comparator_5_eq));  // open: gt, lt
  Comparator #(.width(6), .mode("unsigned")) comparator_6 (
    .a(Code), .b(6'b011011), .eq(comparator_6_eq));  // open: gt, lt
  Comparator #(.width(6), .mode("unsigned")) comparator_7 (
    .a(Code), .b(6'b100100), .eq(comparator_7_eq));  // open: gt, lt
  Comparator #(.width(6), .mode("unsigned")) comparator_8 (
    .a(Code), .b(6'b100101), .eq(comparator_8_eq));  // open: gt, lt
  Comparator #(.width(6), .mode("unsigned")) comparator_9 (
    .a(Code), .b(6'b100110), .eq(comparator_9_eq));  // open: gt, lt
  Comparator #(.width(6), .mode("unsigned")) comparator_10 (
    .a(Code), .b(6'b100111), .eq(comparator_10_eq));  // open: gt, lt
  Comparator #(.width(6), .mode("unsigned")) comparator_11 (
    .a(Code), .b(6'b101010), .eq(comparator_11_eq));  // open: gt, lt
  Comparator #(.width(6), .mode("unsigned")) comparator_12 (
    .a(Code), .b(6'b101011), .eq(comparator_12_eq));  // open: gt, lt
  Comparator #(.width(6), .mode("unsigned")) comparator_13 (
    .a(Code), .b(6'b000010), .eq(comparator_13_eq));  // open: gt, lt
  Priority_Encoder #(.select(4)) priority_encoder_1 (
    .in0(comparator_1_eq), .in1(comparator_2_eq), .in2(comparator_3_eq), .in3(comparator_4_eq),
    .in4(comparator_5_eq), .in5(comparator_6_eq), .in6(comparator_7_eq), .in7(comparator_8_eq),
    .in8(comparator_9_eq), .in9(comparator_10_eq), .in10(comparator_11_eq), .in11(comparator_12_eq),
    .in12(comparator_13_eq), .out(Output));  // open: in13, in14, in15, gs, en_out, en_in
  or or_1 (WHi_Lo, comparator_3_eq, comparator_4_eq, comparator_5_eq, comparator_6_eq);

  // Other names for the same wires on the sheet: Inmediate = in_3

  // Notes on the sheet:
  //   Add
  //   Sub
  //   mult
  //   multu
  //   div
  //   divu
  //   and
  //   or
  //   nor
  //   xor
  //   slt
  //   sltu
  //   random
endmodule

module Branch_Control (
  input  [31:0] PC,
  input  [31:0] Rs,
  input  [25:0] Jump,
  input  [15:0] Offset,
  input  [2:0] ID,
  input  Equal,
  input  NoEqual,
  input  bgtz,
  input  blez,
  input  bltz,
  output [31:0] Next_Program_Counter
);

  wire comparator_1_eq, comparator_2_eq, comparator_3_eq, not_1_out, not_2_out, not_3_out;
  wire [1:0] Selector;
  wire [31:0] and_3_out, and_4_out, not_4_out, PC_4, PC_4_Offset_4, Result;
  wire [31:18] Offset_4;
  wire [31:31] multiplexer_1_out;

  Adder #(.width(32)) adder_1 (.a(PC), .b(32'h4), .out(PC_4));  // open: cin, cout
  assign Offset_4 = {{13{Offset[15]}}, Offset[15]};  // Bit_Extender bit_extender_1
  Adder #(.width(32)) adder_2 (.a({Offset_4, Offset, 2'b00}), .b(PC_4), .out(PC_4_Offset_4));  // open: cin, cout
  // Probe on {Offset_4, Offset, 2'b00}
  // Probe on PC_4_Offset_4
  Comparator #(.width(3)) comparator_1 (.a(ID), .b(3'b001), .eq(comparator_1_eq));  // open: gt, lt
  Comparator #(.width(3)) comparator_2 (.a(ID), .b(3'b010), .eq(comparator_2_eq));  // open: gt, lt
  not not_1 (not_1_out, comparator_3_eq);
  Comparator #(.width(3)) comparator_3 (.a(ID), .b(3'b000), .eq(comparator_3_eq));  // open: gt, lt
  not not_2 (not_2_out, comparator_1_eq);
  not not_3 (not_3_out, comparator_2_eq);
  and and_1 (Selector[1], not_2_out, not_1_out);
  and and_2 (Selector[0], not_3_out, not_1_out);
  Multiplexer #(.select(3)) multiplexer_1 (
    .in0(1'b0), .in1(1'b0), .in2(1'b0), .in3(Equal), .in4(NoEqual), .in5(bgtz), .in6(blez), .in7(bltz),
    .out(multiplexer_1_out[31]), .sel(ID));  // open: en
  assign not_4_out = ~{32{multiplexer_1_out[31]}};  // NOT_Gate not_4, 32 bits wide
  Multiplexer #(.select(2), .width(32)) multiplexer_2 (
    .in0(PC_4), .in1({PC[31:28], Jump, 2'b00}), .in2(Rs), .in3(Result), .out(Next_Program_Counter),
    .sel(Selector));  // open: en
  assign and_3_out = {32{multiplexer_1_out[31]}} & PC_4_Offset_4;  // AND_Gate and_3, 32 bits wide
  assign and_4_out = not_4_out & PC_4;  // AND_Gate and_4, 32 bits wide
  assign Result = and_3_out | and_4_out;  // OR_Gate or_1, 32 bits wide

  // Other names for the same wires on the sheet: J[31:2] = {PC[31:28], Jump}; Next_PC[31:0] = Next_Program_Counter;
  //   Offset_4[17:2] = Offset

  // Notes on the sheet:
  //   INPUTS
  //   Entrada del decoder
  //   Salto Estandar
  //   beq, bne, bltz, bgtz, blez
  //   Jump
  //   00: PC+4 , 01:J , 10: Rs , 11: cualquiera de las otras operaciones endependencia del ID 
  //   Para las últimas 5 instrucciones o es PC+4 o eso sumado al Offset por 4
endmodule

module Sign_Extender (
  input  [15:0] Input,
  output [31:0] Output
);

  // Probe on Input
  // Probe on {{17{Input[15]}}, Input[14:0]}

  assign Output = {{17{Input[15]}}, Input[14:0]};
endmodule

module Instruction_decoder (
  input  [31:0] Instruction,
  input  Enable,
  input  Clock,
  output [5:0] Op_Code,
  output [5:0] Funct_Code,
  output [4:0] out_6,
  output [5:0] I_Funct_Code,
  output [15:0] Offset,
  output [4:0] out_9,
  output [25:0] Destiny,
  output [4:0] out_11,
  output Hi,
  output [2:0] Operation,
  output Inmediate,
  output Unsigned,
  output [2:0] Jump_Code,
  output [1:0] Esp_Code,
  output Pop,
  output SW,
  output LW
);

  wire Aritmetic, beq, bgtz, blez, bltz, bne, comparator_7_eq, comparator_8_eq, comparator_11_eq,
       comparator_12_eq, comparator_13_eq, comparator_14_eq, comparator_15_eq, comparator_16_eq,
       comparator_17_eq, comparator_20_eq, comparator_21_eq, comparator_22_eq, comparator_23_eq,
       comparator_24_eq, comparator_25_eq, comparator_26_eq, comparator_27_eq, comparator_28_eq,
       comparator_32_eq, comparator_33_eq, comparator_34_eq, comparator_35_eq, Esp, Half, I_Op, J, Jr, Jump,
       KBD, Mem, Mult_Div, nop, Op1, Op2, or_2_out, or_3_out, or_4_out, or_7_out, Push, R_Arit, Ram_Mem,
       Register_Move, RND, Sig, TTY, Unsig1, Unsig2, Unsig3;

  Comparator #(.width(6), .mode("unsigned")) comparator_1 (.a(6'b000010), .b(Op_Code), .eq(J));  // open: gt, lt
  Comparator #(.width(6), .mode("unsigned")) comparator_2 (.a(6'b000100), .b(Op_Code), .eq(beq));  // open: gt, lt
  Comparator #(.width(6), .mode("unsigned")) comparator_3 (.a(6'b000101), .b(Op_Code), .eq(bne));  // open: gt, lt
  Comparator #(.width(6), .mode("unsigned")) comparator_4 (.a(6'b000110), .b(Op_Code), .eq(blez));  // open: gt, lt
  Comparator #(.width(6), .mode("unsigned")) comparator_5 (.a(6'b000111), .b(Op_Code), .eq(bgtz));  // open: gt, lt
  Comparator #(.width(6), .mode("unsigned")) comparator_6 (.a(6'b000001), .b(Op_Code), .eq(bltz));  // open: gt, lt
  Comparator #(.width(6), .mode("unsigned")) comparator_7 (
    .a({6{1'b0}}), .b(Destiny[5:0]), .eq(comparator_7_eq));  // open: gt, lt
  Comparator #(.width(6), .mode("unsigned")) comparator_8 (
    .a(6'b001000), .b(Destiny[5:0]), .eq(comparator_8_eq));  // open: gt, lt
  Priority_Encoder priority_encoder_1 (
    .in0(nop), .in1(J), .in2(Jr), .in3(beq), .in4(bne), .in5(blez), .in6(bgtz), .in7(bltz));  // open: out, en_in, gs, en_out
  Register #(.width(32)) register_1 (.D(Instruction), .en(Enable), .Q({Op_Code, Destiny}), .clk(Clock));  // open: clr
  and and_1 (nop, R_Arit, comparator_7_eq);
  and and_2 (Jr, R_Arit, comparator_8_eq);
  or or_1 (Jump, nop, J, Jr, beq, bne, blez, bgtz, bltz);
  Comparator #(.width(6), .mode("unsigned")) comparator_9 (.a({6{1'b0}}), .b(Op_Code), .eq(R_Arit));  // open: gt, lt
  Comparator #(.width(6), .mode("unsigned")) comparator_10 (.a(6'b001111), .b(Destiny[5:0]), .eq(Hi));  // open: gt, lt
  Comparator #(.width(6), .mode("unsigned")) comparator_11 (
    .a(6'b010001), .b(Destiny[5:0]), .eq(comparator_11_eq));  // open: gt, lt
  Comparator #(.width(3), .mode("unsigned")) comparator_12 (
    .a(3'b000), .b(Op_Code[2:0]), .eq(comparator_12_eq));  // open: gt, lt
  Comparator #(.width(3), .mode("unsigned")) comparator_13 (
    .a(3'b100), .b(Op_Code[2:0]), .eq(comparator_13_eq));  // open: gt, lt
  Comparator #(.width(3), .mode("unsigned")) comparator_14 (
    .a(3'b101), .b(Op_Code[2:0]), .eq(comparator_14_eq));  // open: gt, lt
  Comparator #(.width(3), .mode("unsigned")) comparator_15 (
    .a(3'b110), .b(Op_Code[2:0]), .eq(comparator_15_eq));  // open: gt, lt
  Comparator #(.width(3), .mode("unsigned")) comparator_16 (
    .a(3'b010), .b(Op_Code[2:0]), .eq(comparator_16_eq));  // open: gt, lt
  Comparator #(.width(3), .mode("unsigned")) comparator_17 (
    .a(3'b011), .b(Op_Code[2:0]), .eq(comparator_17_eq));  // open: gt, lt
  or or_2 (or_2_out, Hi, comparator_11_eq);
  and and_3 (Register_Move, or_2_out, R_Arit);
  or or_3 (or_3_out, comparator_12_eq, comparator_13_eq, comparator_14_eq);
  and and_4 (Op1, or_3_out, I_Op);
  and and_5 (Op2, I_Op, or_4_out);
  or or_4 (or_4_out, comparator_15_eq, comparator_16_eq, comparator_17_eq);
  or or_5 (Inmediate, Op1, Op2);
  or or_6 (Aritmetic, Inmediate, R_Arit);
  Comparator #(.width(6), .mode("unsigned")) comparator_18 (.a(6'b111000), .b(Op_Code), .eq(Mem));  // open: gt, lt
  Comparator #(.width(3), .mode("unsigned")) comparator_19 (.a(3'b001), .b(Op_Code[5:3]), .eq(I_Op));  // open: gt, lt
  Multiplexer #(.width(3)) multiplexer_1 (
    .in0(Op_Code[2:0]), .in1(3'b000), .out(I_Funct_Code[2:0]), .sel(comparator_20_eq));  // open: en
  Comparator #(.width(3), .mode("unsigned")) comparator_20 (
    .a(3'b110), .b(Op_Code[2:0]), .eq(comparator_20_eq));  // open: gt, lt
  Multiplexer #(.width(3)) multiplexer_2 (.in0(3'b101), .in1(3'b100), .out(I_Funct_Code[5:3]), .sel(Op1));  // open: en
  Comparator #(.width(6)) comparator_21 (.a(Destiny[5:0]), .b(6'b101011), .eq(comparator_21_eq));  // open: gt, lt
  Comparator #(.width(6)) comparator_22 (.a(Op_Code), .b(6'b001011), .eq(comparator_22_eq));  // open: gt, lt
  and and_6 (Unsig2, R_Arit, comparator_21_eq);
  and and_7 (Unsig3, Inmediate, comparator_22_eq);
  Comparator #(.width(6), .mode("unsigned")) comparator_23 (
    .a({6{1'b0}}), .b(Destiny[5:0]), .eq(comparator_23_eq));  // open: gt, lt
  Comparator #(.width(6), .mode("unsigned")) comparator_24 (
    .a(6'b000001), .b(Destiny[5:0]), .eq(comparator_24_eq));  // open: gt, lt
  and and_8 (Pop, Mem, comparator_23_eq);
  and and_9 (Push, Mem, comparator_24_eq);
  or or_7 (or_7_out, Sig, Unsig1);
  Comparator #(.width(6), .mode("unsigned")) comparator_25 (
    .a(6'b011000), .b(Destiny[5:0]), .eq(comparator_25_eq));  // open: gt, lt
  or or_8 (Sig, comparator_25_eq, comparator_26_eq);
  Comparator #(.width(6), .mode("unsigned")) comparator_26 (
    .a(6'b011010), .b(Destiny[5:0]), .eq(comparator_26_eq));  // open: gt, lt
  Comparator #(.width(6), .mode("unsigned")) comparator_27 (
    .a(6'b011001), .b(Destiny[5:0]), .eq(comparator_27_eq));  // open: gt, lt
  or or_9 (Unsig1, comparator_27_eq, comparator_28_eq);
  Comparator #(.width(6), .mode("unsigned")) comparator_28 (
    .a(6'b011011), .b(Destiny[5:0]), .eq(comparator_28_eq));  // open: gt, lt
  and and_10 (Mult_Div, or_7_out, R_Arit);
  Comparator #(.width(6), .mode("unsigned")) comparator_29 (.a(6'b100011), .b(Op_Code), .eq(LW));  // open: gt, lt
  Comparator #(.width(6), .mode("unsigned")) comparator_30 (.a(6'b101011), .b(Op_Code), .eq(SW));  // open: gt, lt
  Priority_Encoder priority_encoder_2 (
    .in0(Jump), .in1(Aritmetic), .in2(Mult_Div), .in3(Register_Move), .in4(Mem), .in5(Ram_Mem), .in6(Esp),
    .out(Operation));  // open: in7, en_in, gs, en_out
  or or_10 (Unsigned, Unsig1, Unsig2, Unsig3);
  or or_11 (Ram_Mem, LW, SW);
  Comparator #(.width(6), .mode("unsigned")) comparator_31 (.a({6{1'b1}}), .b(Op_Code), .eq(Esp));  // open: gt, lt
  Comparator #(.width(6), .mode("unsigned")) comparator_32 (
    .a({6{1'b1}}), .b(Destiny[5:0]), .eq(comparator_32_eq));  // open: gt, lt
  Comparator #(.width(6), .mode("unsigned")) comparator_33 (
    .a(6'b000001), .b(Destiny[5:0]), .eq(comparator_33_eq));  // open: gt, lt
  Comparator #(.width(6), .mode("unsigned")) comparator_34 (
    .a(6'b000010), .b(Destiny[5:0]), .eq(comparator_34_eq));  // open: gt, lt
  Comparator #(.width(6), .mode("unsigned")) comparator_35 (
    .a(6'b001000), .b(Destiny[5:0]), .eq(comparator_35_eq));  // open: gt, lt
  Priority_Encoder #(.select(2)) priority_encoder_3 (
    .in0(Half), .in1(TTY), .in2(RND), .in3(KBD), .out(Esp_Code));  // open: gs, en_out, en_in
  and and_11 (Half, Esp, comparator_32_eq);
  and and_12 (TTY, Esp, comparator_33_eq);
  and and_13 (RND, Esp, comparator_34_eq);
  and and_14 (KBD, Esp, comparator_35_eq);

  assign Funct_Code = Destiny[5:0];
  assign Offset = Destiny[15:0];
  assign out_6 = Destiny[25:21];
  assign out_9 = Destiny[20:16];
  assign out_11 = Destiny[15:11];

  // Other names for the same wires on the sheet: FUNC_CODE[5:0] = Destiny[5:0]; X[4:0] = Destiny[10:6];
  //   RD[4:0] = Destiny[15:11]; RS[4:0] = Destiny[20:16]; RT[4:0] = Destiny[25:21]; I_Instr[2:0] = Op_Code[2:0];
  //   OP[5:0] = Op_Code; I_Type[2:0] = Op_Code[5:3]; Inmediato = Inmediate; LoadWord = LW; StoreWord = SW;
  //   Unsig = Unsigned

  // Notes on the sheet:
  //   Tipo J
  //   Salto
  //   Nop
  //   Salto
  //   Mover Registros
  //   Aritmetica-R
  //   Identificar operacion inmediata
  //   I-Instruction Split
  //   R-Memory
  //   I Type (Empiezan 001)
  //   Aritm-Logic-Comp
  //   Conv Inmediato a R-Funct-Code
  //   Pop
  //   Push
  //   I-Memory
  //   Special
  //   Half
  //   TTY
  //   RND
  //   KBD
endmodule

module Add_Circuit (
  input  [31:0] A,
  input  [31:0] B,
  output [31:0] Output,
  output OverFlow,
  output C_out
);

  wire adder_1_cout;

  // Probe on A
  // Probe on B
  Adder #(.width(31)) adder_1 (.a(A[30:0]), .b(B[30:0]), .out(Output[30:0]), .cout(adder_1_cout));  // open: cin
  Adder #(.width(1)) adder_2 (.a(A[31]), .b(B[31]), .out(Output[31]), .cin(adder_1_cout), .cout(C_out));
  xor xor_1 (OverFlow, adder_1_cout, C_out);
  // Probe on Output
endmodule

module Sub_Circuit (
  input  [31:0] A,
  input  [31:0] B,
  output [31:0] Output,
  output OverFlow,
  output B_out
);

  wire adder_1_cout;
  wire [31:0] not_1_out;

  // Probe on A
  // Probe on B
  assign not_1_out = ~B;  // NOT_Gate not_1, 32 bits wide
  Adder #(.width(31)) adder_1 (.a(A[30:0]), .b(not_1_out[30:0]), .out(Output[30:0]), .cin(1'b1), .cout(adder_1_cout));
  Adder #(.width(1)) adder_2 (.a(A[31]), .b(not_1_out[31]), .out(Output[31]), .cin(adder_1_cout), .cout(B_out));
  xor xor_1 (OverFlow, adder_1_cout, B_out);
  // Probe on Output
endmodule

module Sign_Mult (
  input  [31:0] A,
  input  [31:0] B,
  output [31:0] Output1,
  output Output,
  output [31:0] Output2
);

  wire and_1_out, comparator_1_eq, comparator_2_eq, modulo_1_sign, modulo_2_sign, or_1_out, xor_1_out;
  wire [31:0] adder_1_out, adder_2_out, modulo_1_output, modulo_2_output, multiplier_1_cout,
       multiplier_1_out, not_1_out, not_2_out;

  Modulo modulo_1 (.Input(B), .Sign(modulo_1_sign), .Output(modulo_1_output));
  Modulo modulo_2 (.Input(A), .Sign(modulo_2_sign), .Output(modulo_2_output));
  Comparator #(.width(32)) comparator_1 (.a(A), .b({32{1'b0}}), .eq(comparator_1_eq));  // open: gt, lt
  Comparator #(.width(32)) comparator_2 (.a({32{1'b0}}), .b(B), .eq(comparator_2_eq));  // open: gt, lt
  Multiplier #(.width(32)) multiplier_1 (
    .a(modulo_2_output), .b(modulo_1_output), .out(multiplier_1_out), .cout(multiplier_1_cout));  // open: cin
  xor xor_1 (xor_1_out, modulo_2_sign, modulo_1_sign);
  and and_1 (and_1_out, xor_1_out, ~or_1_out);  // AND_Gate
  or or_1 (or_1_out, comparator_1_eq, comparator_2_eq);
  assign not_1_out = ~multiplier_1_out;  // NOT_Gate not_1, 32 bits wide
  assign not_2_out = ~multiplier_1_cout;  // NOT_Gate not_2, 32 bits wide
  Adder #(.width(32)) adder_1 (.a(not_1_out), .b(32'h1), .out(adder_1_out), .cout(Output));  // open: cin
  Adder #(.width(32)) adder_2 (.a(not_2_out), .b({32{1'b0}}), .out(adder_2_out), .cin(Output));  // open: cout
  Multiplexer #(.width(32)) multiplexer_1 (
    .in0(multiplier_1_out), .in1(adder_1_out), .out(Output1), .sel(and_1_out));  // open: en
  Multiplexer #(.width(32)) multiplexer_2 (
    .in0(multiplier_1_cout), .in1(adder_2_out), .out(Output2), .sel(and_1_out));  // open: en
endmodule

module Modulo (
  input  [31:0] Input,
  output [31:0] Output,
  output Sign
);

  wire [31:0] negator_1_out;

  Negator #(.width(32)) negator_1 (.in(Input), .out(negator_1_out));
  Multiplexer #(.width(32)) multiplexer_1 (
    .in0(Input), .in1(negator_1_out), .out(Output), .sel(Input[31]));  // open: en

  assign Sign = Input[31];
endmodule
